// Logisim project SynthBite16.circ as structural Verilog: 1 circuit, main circuit main
module main (
);

  wire AC_p1, AC_p2, AC_p3, AC_p5, AC_p6, AC_p7, AC_p8, AC_p9, AC_p10, AC_p11, AC_p12, AC_p13, AC_p14,
       AC_p15, AC_p16, AC_p17, AC_p18, AC_p19, AC_p20, AC_p21, AC_p22, AC_p23, AC_p24, AC_p25, AC_p26,
       AC_p27, AC_p28, AC_p29, controlled_buffer_13_out, controlled_buffer_14_out, controlled_buffer_15_out,
       controlled_buffer_16_out, decoder_1_out0, decoder_1_out1, decoder_2_out0, MasterClock_out, undriven,
       undriven_2, undriven_3, undriven_4, undriven_7, undriven_8, undriven_9, undriven_10, undriven_11,
       undriven_12, undriven_13, undriven_14, undriven_15, undriven_16, undriven_17, undriven_18,
       undriven_19, undriven_20, undriven_21, undriven_22;
  wire [3:0] undriven_23, undriven_24;
  wire [9:0] undriven_5;
  wire [11:0] register_1_q;
  wire [15:0] MEM_data;
  wire [23:0] CNTRL_MEM_data, register_1_q_2;
  wire [35:24] undriven_6;

  Clock MasterClock (.out(MasterClock_out));
  LED led_1 (.in(MasterClock_out));
  DotMatrix #(.matrixcols(16), .matrixrows(1)) dotmatrix_1 (
    .col0(controlled_buffer_16_out), .col1(controlled_buffer_15_out), .col2(controlled_buffer_14_out),
    .col3(controlled_buffer_13_out), .col4(AC_p17), .col5(AC_p16), .col6(AC_p15), .col7(AC_p14),
    .col8(AC_p13), .col9(AC_p12), .col10(AC_p11), .col11(AC_p10), .col12(AC_p9), .col13(AC_p8),
    .col14(AC_p7), .col15(AC_p6));
  // Shift_Register #(.length(16)) AC: pin names not known; wires that end beside it: AC_p1, AC_p2, AC_p3, MasterClock_out, AC_p5, AC_p6, AC_p7, AC_p8, AC_p9, AC_p10, AC_p11, AC_p12, AC_p13, AC_p14, AC_p15, AC_p16, AC_p17, AC_p18, AC_p19, AC_p20, AC_p21, AC_p22, AC_p23, AC_p24, AC_p25, AC_p26, AC_p27, AC_p28, AC_p29
  assign AC_p6 = decoder_1_out1 ? AC_p18 : 1'bz;  // Controlled_Buffer controlled_buffer_1
  assign AC_p7 = decoder_1_out1 ? AC_p19 : 1'bz;  // Controlled_Buffer controlled_buffer_2
  assign AC_p8 = decoder_1_out1 ? AC_p20 : 1'bz;  // Controlled_Buffer controlled_buffer_3
  assign AC_p9 = decoder_1_out1 ? AC_p21 : 1'bz;  // Controlled_Buffer controlled_buffer_4
  assign AC_p10 = decoder_1_out1 ? AC_p22 : 1'bz;  // Controlled_Buffer controlled_buffer_5
  assign AC_p11 = decoder_1_out1 ? AC_p23 : 1'bz;  // Controlled_Buffer controlled_buffer_6
  assign AC_p12 = decoder_1_out1 ? AC_p24 : 1'bz;  // Controlled_Buffer controlled_buffer_7
  assign AC_p13 = decoder_1_out1 ? AC_p25 : 1'bz;  // Controlled_Buffer controlled_buffer_8
  assign AC_p14 = decoder_1_out1 ? AC_p26 : 1'bz;  // Controlled_Buffer controlled_buffer_9
  assign AC_p15 = decoder_1_out1 ? AC_p27 : 1'bz;  // Controlled_Buffer controlled_buffer_10
  assign AC_p16 = decoder_1_out1 ? AC_p28 : 1'bz;  // Controlled_Buffer controlled_buffer_11
  assign AC_p17 = decoder_1_out1 ? AC_p29 : 1'bz;  // Controlled_Buffer controlled_buffer_12
  assign controlled_buffer_13_out = decoder_1_out1 ? undriven : 1'bz;  // Controlled_Buffer controlled_buffer_13
  assign controlled_buffer_14_out = decoder_1_out1 ? undriven_2 : 1'bz;  // Controlled_Buffer controlled_buffer_14
  assign controlled_buffer_15_out = decoder_1_out1 ? undriven_3 : 1'bz;  // Controlled_Buffer controlled_buffer_15
  assign controlled_buffer_16_out = decoder_1_out1 ? undriven_4 : 1'bz;  // Controlled_Buffer controlled_buffer_16
  ROM #(.addrWidth(10), .dataWidth(24), .misaligned("true")) CNTRL_MEM (.addr(undriven_5), .data(CNTRL_MEM_data));
  Register #(.trigger("falling"), .width(36)) register_1 (
    .D({undriven_6, CNTRL_MEM_data}), .en(1'b1), .clk(MasterClock_out), .Q({register_1_q, register_1_q_2}));  // open: clr
  DotMatrix #(.matrixcols(24), .matrixrows(1)) dotmatrix_2 (
    .col0(undriven_23[0]), .col1(undriven_23[1]), .col2(undriven_23[2]), .col3(undriven_23[3]),
    .col4(undriven_24[0]), .col5(undriven_24[1]), .col6(undriven_24[2]), .col7(undriven_24[3]),
    .col8(undriven_22), .col9(undriven_7), .col10(undriven_8), .col11(undriven_9), .col12(undriven_10),
    .col13(undriven_11), .col14(undriven_12), .col15(undriven_13), .col16(undriven_14), .col17(undriven_15),
    .col18(undriven_16), .col19(undriven_17), .col20(undriven_18), .col21(undriven_19), .col22(undriven_20),
    .col23(undriven_21));
  Decoder #(.select(4)) decoder_1 (
    .out0(decoder_1_out0), .out1(decoder_1_out1), .sel(undriven_23), .en(undriven_22));  // open: out2, out3, out4, out5, out6, out7, out8, out9, out10, out11, out12, out13, out14, out15
  Decoder #(.select(4)) decoder_2 (
    .out0(decoder_2_out0), .out1(AC_p2), .sel(undriven_24), .en(undriven_7));  // open: out2, out3, out4, out5, out6, out7, out8, out9, out10, out11, out12, out13, out14, out15
  RAM #(.addrWidth(12), .dataWidth(16), .databus("bidir")) MEM (
    .addr(undriven_6), .we(decoder_2_out0), .oe(decoder_1_out0), .clk(MasterClock_out), .data(MEM_data));

  // Notes on the sheet:
  //   CLOCK
  //   PRESENT BUS VALUES
  //   SYSTEM BUS
  //   16 LINES
  //   ACCUMULATOR
  //   LEAST SIGNIFICANT LINE
  //   MOST SIGNIFICANT LINE
  //   ALU
  //   CONTROL MEMORY
  //   CONTROL UNIT
  //   PRESENT CONTROL
  //   MEM OUT ENABLE
  //   ACC ON BUS
  //   PUT ON BUS
  //   MEM WRITE ENABLE
  //   AC PARLLEL LOAD
  //   AC RESET ASYNC
  //   ACC SHIFT
  //   ACC SERIAL IN
  //   LOAD FROM BUS
  //   MAIN MEMORY
endmodule
